# Fritzing sketch ESP32_Lighting_Capture_basic_0.0.3 (saved by Fritzing 0.9.3b)

parts:
  U1 = Wemos Lolin D32
  U2 = SWITCH_SPDT [package=kps-1290]
  U3 = LIPO-110mAh [package=lipo-110]
  Part2 = Light Sensor
  LED1 = LED - 5mm [color="Red (633nm)" package="5 mm [THT]"]  # not connected
  LED2 = LED - 5mm [color="Red (633nm)" package="5 mm [THT]"]  # not connected
  LED3 = LED - 5mm [color="Red (633nm)" package="5 mm [THT]"]  # not connected
  U4 = 3.5mm Audio Jack [package=audio-jack-3.5mm-smd]  # not connected

nets:
  N1: U1.pin_0, Part2.no_name_yet#connectorRXD-1
  N2: U1.pin_5, Part2.no_name_yet#connectorUARTGND-1
  N3: U1.pin_16, U2.S
  N4: U1.pin_17, U3.-
  N5: U1.pin_33, Part2.no_name_yet#connectorUARTVCC-0
  N6: U2.P, U3.+

notes:
  Li-Po
  1000mAh
  Lighning Capture for camera
  Basic
  V 1.0.0.3
  On/Off
  Switch
  INPUT OUT
  - ISOLATOR FOCUS -
  GND GND
  INPUT OUT
  - ISOLATOR SHUTTER -
  GND GND
  Green (OPTIONAL)
  Yellow TRAFFIC
  Red LIGHT
  Black MODULE
  OPTIONAL
  BATTERY
  Battery is charged from on-board charger.
  Can also be powered directly from
  USB Socket
  3.5MM Jack Socket.
  Body - Black
  Collar - Yellow
  Tip - Green
  Light Sensor Module

custom parts:
  Wemos Lolin D32: Wemos Lolin D32 wifi and blue tooth board based on the ESP-32 cpu, digital I/Os 22, analog inputs 6, analog outputs 2 clock 240mhz, Flash 4Mbytes, lipo battery charger (500ma connection broken out on breadboard but not pcb), usb. The mounting holes are only set on the silkscreen, if you want actual holes in the pcb copy the hole from the pcb menu in parts over the top of the hole in the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
